# Fritzing sketch Clessidra digitale hardware (saved by Fritzing 0.9.3b)
breadboards: 1

parts:
  Componente1 = Arduino Uno (Rev3)
  S1 = Tilt Switch [package=THT]
  R1 = Resistor [tolerance=±5% resistance=220 package="0805 [SMD]"]
  LED1 = smd LED [color="Red (633nm)" package="1206 [SMD]"]
  R2 = Resistor [tolerance=±5% resistance=220 package="0805 [SMD]"]
  LED2 = smd LED [color="Red (633nm)" package="1206 [SMD]"]
  R3 = Resistor [tolerance=±5% resistance=220 package="0805 [SMD]"]
  LED3 = smd LED [color="Red (633nm)" package="1206 [SMD]"]
  R4 = Resistor [tolerance=±5% resistance=220 package="0805 [SMD]"]
  LED4 = smd LED [color="Red (633nm)" package="1206 [SMD]"]
  LED5 = smd LED [color="Red (633nm)" package="1206 [SMD]"]
  LED6 = smd LED [color="Red (633nm)" package="1206 [SMD]"]
  R5 = Resistor [tolerance=±5% resistance=220 package="0805 [SMD]"]
  R6 = Resistor [tolerance=±5% resistance=220 package="0805 [SMD]"]
  R7 = Resistor [tolerance=±5% resistance=220 package="0805 [SMD]"]

nets:
  N1: Componente1.D8, S1.Pin_2, R1.Pin_0
  N2: Componente1.D2, LED6.anode
  N3: Componente1.D3_PWM, LED5.anode
  N4: Componente1.D4, LED4.anode
  N5: Componente1.D5_PWM, LED3.anode
  N6: Componente1.D6_PWM, LED2.anode
  N7: Componente1.D7, LED1.anode
  N8: Componente1.5V, S1.Pin_1
  N9: Componente1.GND, R1.Pin_1, R2.Pin_1, R4.Pin_1, R5.Pin_1, R6.Pin_1, R7.Pin_1
  N10: LED1.cathode, R2.Pin_0
  N11: LED2.cathode, R3.Pin_0
  N12: LED3.cathode, R4.Pin_0
  N13: LED4.cathode, R5.Pin_0
  N14: LED5.cathode, R6.Pin_0
  N15: LED6.cathode, R7.Pin_0

notes:
  La resistenza posta sull'interruttore di inclinazione è di 10 KOhm.

// code stored in the sketch: Clessidra_digitale_software.ino
const int Interruttore_Pin = 8;                                                                       //Pin interruttore di inclinazione.
unsigned long Tempo_Ultimo_Led = 0;                                                                   //Variabile che memorizza il momento in cui e' stato modificato l'ultimo led.
int Stato_Interruttore = 0;                                                                           //Memorizza lo stato dell'interruttore.
int Precedente_Stato_Interruttore = 0;                                                                //Memorizza il precedente stato dell'interruttore.

int Led = 2;                                                                                          //Variabile usata per verificare quale led e' il prossimo ad accendersi.
long Intervallo_Di_Tempo = 3000;                                                                      //Intervallo di accensione di ogni led.

void setup()
{
  for(int x = 2;x<8;x++)                                                                               //Dichiara i pin OUTPUT con un ciclo for.
  {
    pinMode(x, OUTPUT);
  }
  pinMode(Interruttore_Pin, INPUT);
}

void loop()
{
  unsigned long Tempo_Attuale = millis();                                                               //Cronometra il tempo da quando Arduino si e' acceso o resettato.
  if(Tempo_Attuale - Tempo_Ultimo_Led > Intervallo_Di_Tempo)                                            //Controlla se e' passato abbastanza tempo per accendere il led successivo. 
  {
    Tempo_Ultimo_Led = Tempo_Attuale;                                                                   //Se si' imposta la prima variabile al valore della seconda.
    digitalWrite(Led, HIGH);
    Led++;                                                                                              //Incrementa la variabile Led.
    
  if(Led == 7)                                                                                          //Controlla se il led sul pin 7 e' acceso.
  {
    }
  }
  Stato_Interruttore = digitalRead(Interruttore_Pin);                                                   //Memorizza lo stato attuale dell'interruttore.
    

  if(Stato_Interruttore != Precedente_Stato_Interruttore)                                               //Se lo stato dell'interruttore e' diverso dal precedente: 
  {
    for(int x = 2; x<8;x++){                                                                            //Spegni tutti i led.
      digitalWrite(x, LOW);
    }
    Led = 2;
    Tempo_Ultimo_Led = Tempo_Attuale;
  }
  Precedente_Stato_Interruttore = Stato_Interruttore;
}
