# Fritzing sketch LED RGB hardware (saved by Fritzing 0.9.3b)
breadboards: 1

parts:
  Componente1 = Arduino Uno (Rev3)
  LED1 = RGB LED (com. cathode, rbg) [package="5 mm [THT]"]
  R1 = PHOTOCELL [package=photocell-kit]
  R2 = PHOTOCELL [package=photocell-kit]
  R3 = PHOTOCELL [package=photocell-kit]
  R4 = Resistor [tolerance=±5% resistance=220 package="0402 [SMD]"]
  R5 = Resistor [tolerance=±5% resistance=220 package="0402 [SMD]"]
  R6 = Resistor [tolerance=±5% resistance=220 package="0402 [SMD]"]
  R7 = Resistor [tolerance=±5% resistance=220 package="0402 [SMD]"]
  R8 = Resistor [tolerance=±5% resistance=220 package="0402 [SMD]"]
  R9 = Resistor [tolerance=±5% resistance=220 package="0402 [SMD]"]

nets:
  N1: Componente1.A0, R3.P$2, R6.Pin_0
  N2: Componente1.A1, R2.P$2, R5.Pin_0
  N3: Componente1.A2, R1.P$2, R4.Pin_0
  N4: Componente1.D9_PWM, R9.Pin_1
  N5: Componente1.D10_PWM/SS, R8.Pin_1
  N6: Componente1.D11_PWM/MOSI, R7.Pin_1
  N7: Componente1.5V, R1.P$1, R2.P$1, R3.P$1
  N8: Componente1.GND, LED1.common_cathode, R4.Pin_1, R5.Pin_1, R6.Pin_1
  N9: LED1.red_anode, R7.Pin_0
  N10: LED1.blue_anode, R8.Pin_0
  N11: LED1.green_anode, R9.Pin_0

notes:
  Le tre resistenze sono da 10 KOhm.

// code stored in the sketch: LED_RGB_software.ino
const int Pin_Led_Verde = 9;
const int Pin_Led_Rosso = 11;
const int Pin_Led_Blu = 10;

const int Pin_Sensore_Rosso = A0;
const int Pin_Sensore_Verde = A1;
const int Pin_Sensore_Blu = A2;

int Valore_Rosso = 0;
int Valore_Verde = 0;
int Valore_Blu = 0;

int Valore_Sensore_Rosso = 0;
int Valore_Sensore_Verde = 0;
int Valore_Sensore_Blu = 0;

void setup()
{
  Serial.begin(9600);                                                     //Apre la comunicazione seriale con il computer.
  pinMode(Pin_Led_Verde, OUTPUT);
  pinMode(Pin_Led_Rosso, OUTPUT);
  pinMode(Pin_Led_Blu, OUTPUT);
}

void loop()
{
  Valore_Sensore_Rosso = analogRead(Pin_Sensore_Rosso);
  delay(5);
  Valore_Sensore_Verde = analogRead(Pin_Sensore_Verde);
  delay(5);
  Valore_Sensore_Blu = analogRead(Pin_Sensore_Blu);

  Valore_Rosso = Valore_Sensore_Rosso/4;                                  //Divide per quattro la lettura dei sensori.
  Valore_Verde = Valore_Sensore_Verde/4;
  Valore_Blu = Valore_Sensore_Blu/4;

  Serial.print("\n Valori\t Rosso: ");
  Serial.print(Valore_Rosso);
  Serial.print("\t Verde: ");
  Serial.print(Valore_Verde);
  Serial.print("\t Blu: ");
  Serial.print(Valore_Blu);

  analogWrite(Pin_Led_Rosso, Valore_Rosso);
  analogWrite(Pin_Led_Verde, Valore_Verde);
  analogWrite(Pin_Led_Blu, Valore_Blu);
  }
