# Fritzing sketch Motore a corrente continua hardware (saved by Fritzing 0.9.3b)
breadboards: 1

parts:
  Componente1 = Arduino Uno (Rev3)
  S1 = Pushbutton [package="[SMD]"]
  R1 = Resistor [tolerance=±5% resistance=220 package="2010 [SMD]"]
  Q1 = MOSFET-NCHANNEL [package=to220v]
  D1 = Schottky Diode [part_number=1N5817 package="Melf DO-213 AB [SMD]"]
  M1 = DC Motor
  VCC1 = Battery block 9V

nets:
  N1: Componente1.D9_PWM, Q1.G
  N2: Componente1.D2, S1.Pin_1, S1.Pin_2, R1.Pin_0
  N3: Componente1.5V, S1.Pin_3, S1.Pin_4
  N4: Componente1.GND, R1.Pin_1, Q1.S, VCC1.-
  N5: Q1.D, M1.pin_2
  N6: D1.cathode, M1.pin_1, VCC1.+

notes:
  La resistenza collegata al pulsante è da 10 kOhm.

// code stored in the sketch: Motore_a_corrente_continua_software.ino
const int Pin_Pulsante = 2;                     //Dichiarazione pin del pulsante.
const int Pin_Motore = 9;                       //Dichiarazione pin del motore.
int Stato_Pulsante = 0;                         //Variabile per memorizzare il valore del pulsante.

void setup()
{
  pinMode(Pin_Motore, OUTPUT);                  //Pin motore OUTPUT.
  pinMode(Pin_Pulsante, INPUT);                 //Pin pulsante INPUT.
}

void loop()
{
  Stato_Pulsante = digitalRead(Pin_Pulsante);   //Controlla lo stato del pulsante.

  if (Stato_Pulsante == HIGH) 
  {                                             //Se il pulsante è premuto, il pin viene impostato come HIGH.
    digitalWrite(Pin_Motore, HIGH);       
  }
  else 
  {
    digitalWrite(Pin_Motore, LOW);              //Se il pulsante non è premuto, il pin viene impostato come LOW.
  } 
}
