# Fritzing sketch Motore a corrente continua 2 hardware (saved by Fritzing 0.9.3b)
breadboards: 1

parts:
  Componente1 = Arduino Uno (Rev3)
  S1 = Pushbutton [package="[SMD]"]
  S2 = Pushbutton [package="[SMD]"]
  IC1 = H-Bridge [package=THT]
  U1 = POT [package=pot_alpha_rv16af-20]  # not connected
  M1 = DC Motor
  VCC1 = Battery block 9V
  R1 = Resistor [tolerance=±5% resistance=220 package="0805 [SMD]"]
  R2 = Resistor [tolerance=±5% resistance=220 package="0805 [SMD]"]

nets:
  N1: Componente1.D9_PWM, IC1.1_2EN
  GND: Componente1.GND, IC1.GND1, IC1.GND2, VCC1.-, R1.Pin_0, R2.Pin_0
  N2: Componente1.D2, IC1.2A
  N3: Componente1.D3_PWM, IC1.1A
  N4: Componente1.D4, S2.Pin_1, S2.Pin_2, R2.Pin_1
  N5: Componente1.D5_PWM, S1.Pin_1, S1.Pin_2, R1.Pin_1
  N6: Componente1.5V, S1.Pin_3, S1.Pin_4, S2.Pin_3, S2.Pin_4, IC1.VCC1
  N7: IC1.1Y, M1.pin_1
  N8: IC1.2Y, M1.pin_2

notes:
  Le due resistenze poste sui pulsanti sono da 10 KOhm.
