# Fritzing sketch Serratura arduino hardware (saved by Fritzing 0.9.3b)
breadboards: 1

parts:
  Componente1 = Arduino Uno (Rev3)
  LED1 = LED - 5mm [color="Red (633nm)" package="5 mm [THT]"]
  LED2 = LED - 5mm [color="Red (633nm)" package="5 mm [THT]"]
  LED3 = LED - 5mm [color="Red (633nm)" package="5 mm [THT]"]
  S1 = Pushbutton [package="[THT]"]
  R1 = Resistor [tolerance=±5% resistance=220 package=THT]
  J1 = Piezo Speaker
  R2 = Resistor [tolerance=±5% resistance=220 package=THT]
  R3 = Resistor [tolerance=±5% resistance=220 package=THT]
  R4 = Resistor [tolerance=±5% resistance=220 package=THT]
  R5 = Resistor [tolerance=±5% resistance=220 package=THT]
  J2 = Basic Servo
  C2 = Electrolytic Capacitor [capacitance=10μF package="0605 [SMD, electrolytic]"]

nets:
  N1: Componente1.A0, J1.pin1, R2.Pin_0
  N2: Componente1.D9_PWM, J2.pulse
  N3: Componente1.D2, S1.Pin_1, S1.Pin_2, R1.Pin_1
  5V: Componente1.5V, S1.Pin_3, S1.Pin_4, J1.pin2, J2.vcc, C2.+
  GND: Componente1.GND, LED1.cathode, LED2.cathode, LED3.cathode, R1.Pin_0, R2.Pin_1, J2.gnd, C2.-
  N4: LED1.anode, R5.Pin_0
  N5: LED2.anode, R3.Pin_0
  N6: LED3.anode, R4.Pin_0

notes:
  La resistenza posta sul piezo è da 1MOhm.
  La resistenza posta sulla sinistra è da 10KOhm.
  Per una migliore comunicazione visiva, i led sono di colore giallo, rosso e verde.
  Il condensatore è da 100 uF.

// code stored in the sketch: Serratura_arduino_software.ino
#include <Servo.h>
Servo Servomotore;

const int Piezo = A0;
const int Pin_Interruttore = 2;
const int Led_Giallo = 3;
const int Led_Verde = 4;
const int Led_Rosso = 5;

int Valore_Vibrazione;
int Valore_Pulsante;

const int Vibrazione_Bassa = 10;
const int Vibrazione_Alta = 100;

boolean Blocco = false;
int Numero_Di_Vibrazioni = 0;

void setup(){
  Servomotore.attach(9);
  pinMode(Led_Giallo, OUTPUT);
  pinMode(Led_Rosso, OUTPUT);
  pinMode(Led_Verde, OUTPUT);
  pinMode(Pin_Interruttore, INPUT);
  Serial.begin(9600);
  digitalWrite(Led_Verde, HIGH);
  Servomotore.write(0);
  Serial.println("La serratura e' sbloccata!");
}

void loop(){
  if(Blocco == false) {
    Valore_Pulsante = digitalRead(Pin_Interruttore);
    if(Valore_Pulsante == HIGH){
      Blocco = true;
      digitalWrite(Led_Verde, LOW);
      digitalWrite(Led_Rosso, HIGH);
      Servomotore.write(180);
      Serial.println("La serratura e' bloccata!");
      delay (1000);
      
    }
  }
  if(Blocco == true){
    Valore_Vibrazione = analogRead(Piezo);
    if(Numero_Di_Vibrazioni < 3 && Valore_Vibrazione >0){
      if(checkForKnock(Valore_Vibrazione) == true){
        Numero_Di_Vibrazioni++;
      }
      Serial.print(3-Numero_Di_Vibrazioni);
      Serial.println(" vibrazioni per sbloccare!");
    }
    if(Numero_Di_Vibrazioni >= 3){
      Blocco = false;
      Servomotore.write(0);
      delay(20);
      digitalWrite(Led_Verde, HIGH);
      digitalWrite(Led_Rosso, LOW);
      Serial.println("La serratura e' sbloccata!");
    }
  }
}
boolean checkForKnock(int value){
  if(value > Vibrazione_Bassa && value < Vibrazione_Alta){
    digitalWrite(Led_Giallo, HIGH);
    delay(50);
    digitalWrite(Led_Giallo, LOW);
    Serial.print("Valid knock of value ");
    Serial.println(value);
    return true;
  }
  else{
    Serial.print("Bad knock value ");
    Serial.println(value);
    return false;
  }
}
