# Fritzing sketch Sfera di cristallo hardware (saved by Fritzing 0.9.3b)
breadboards: 1

parts:
  Componente1 = Arduino Uno (Rev3)
  S1 = Momentary Switch [package=ksa_sealed_tac_switch]
  R1 = Resistor [tolerance=±5% resistance=220 package="2512 [SMD]"]
  U1 = POT [package=pot_mammoth]  # not connected
  LCD1 = LCD screen
  R2 = Resistor [tolerance=±5% resistance=220 package="2512 [SMD]"]

nets:
  N1: Componente1.D11_PWM/MOSI, LCD1.E
  N2: Componente1.D12/MISO, LCD1.RS
  N3: Componente1.D2, LCD1.DB7
  N4: Componente1.D3_PWM, LCD1.DB6
  N5: Componente1.D4, LCD1.DB5
  N6: Componente1.D5_PWM, LCD1.DB4
  N7: Componente1.D6_PWM, S1.2, R1.Pin_0
  5V: Componente1.5V, S1.4, LCD1.VDD, R2.Pin_1
  GND: Componente1.GND, R1.Pin_1, LCD1.VSS, LCD1.R/W, LCD1.LED-
  N8: LCD1.LED+, R2.Pin_0

notes:
  La resistenza a sinistra è da 10KOhm.

// code stored in the sketch: Sfera_di_cristallo_software.ino
#include <LiquidCrystal.h>                                                            //Importa la libreria LiquidCrystal.
LiquidCrystal lcd(12, 11, 5, 4, 3, 2);                                                //Dichiarazione pin utilizzati dallo schermo LCD.

const int Pin_Interruttore = 6;                                                       //Pin 6 = Interruttore.
int Stato_Interruttore = 0;                                                           //Stato interruttore.
int Precedente_Stato_Interruttore = 0;                                                //Precedente stato interruttore.
int Risposta;                                                                         //Risposta della sfera.

void setup() 
{
  lcd.begin(16, 2);                                                                   //Specifica la larghezza dello schermo.
  pinMode(Pin_Interruttore, INPUT);                                                   //L'interruttore viene usato come input.
  lcd.print("Interroga");                                                             //Scrive sul display.                                                            
  lcd.setCursor(0, 1);                                                                //Posiziona il cursore in base alle coordinate.
  lcd.print("la sfera!");                                                             //Scrive sul display.
}

void loop()
{
  Stato_Interruttore = digitalRead(Pin_Interruttore);                                 //Lettura dello stato dell'interruttore.
  if (Stato_Interruttore != Precedente_Stato_Interruttore)                            //Se e' diverso il valore delle due variabili...
  {
    if (Stato_Interruttore == LOW)                                                    //Se e' LOW sceglie una risposta a caso.
    {
      Risposta = random(8);
      lcd.clear();                                                                    //Pulisce lo schermo.
      lcd.setCursor(0, 0);                                                            //Posiziona il cursore in base alle coordinate.
      lcd.print("La sfera dice:");                                                    //Scrive sul display.
      lcd.setCursor(0, 1);                                                            //Posiziona il cursore.
      switch(Risposta)                                                                //Esegue diversi pezzi di codice a seconda del parametro specificato.
    {
      case 0:
      lcd.print("Si.");
      break;
      case 1:
      lcd.print("Probabile.");
      break;
      case 2:
      lcd.print("Certo.");
      break;
      case 3:
      lcd.print("Bene.");
      break;
      case 4:
      lcd.print("Forse.");
      break;
      case 5:
      lcd.print("Chiedi ancora.");
      break;
      case 6:
      lcd.print("Improbabile.");
      break;
      case 7:
      lcd.print("No.");
      break;
    }
  }
}
Precedente_Stato_Interruttore = Stato_Interruttore;                                     //Assegna lo stesso valore alle due variabli per il loop successivo.
}
