# Fritzing sketch Servomotore hardware (saved by Fritzing 0.9.3b)
breadboards: 1

parts:
  Componente1 = Arduino Uno (Rev3)
  C1 = Electrolytic Capacitor [capacitance=1μF package="0405 [SMD, electrolytic]"]
  U1 = POT [package=pot_mammoth]  # not connected
  J1 = Basic Servo
  C2 = Electrolytic Capacitor [capacitance=10μF package="0605 [SMD, electrolytic]"]

nets:
  N1: Componente1.D9_PWM, J1.pulse
  5V: Componente1.5V, C1.+, J1.vcc, C2.+
  GND: Componente1.GND, C1.-, J1.gnd, C2.-

notes:
  I due condensatori usati sono entrambi da 100 uF

// code stored in the sketch: Servomotore_software.ino
#include <Servo.h>

Servo Servomotore;

int const Potenziometro = A0;
int Potenziometro_Valore;
int Angolo;

void setup() {
  Servomotore.attach(9);

  Serial.begin(9600);
}

void loop() {
  Potenziometro_Valore = analogRead(Potenziometro);
  Serial.print("\t Potenziometro Valore: ");
  Serial.print(Potenziometro_Valore);
  Angolo = map(Potenziometro_Valore, 0, 1023, 0, 179);
  Serial.print("\n Angolo: ");
  Serial.print(Angolo);

  Servomotore.write(Angolo);
  delay(15);
}
