# Fritzing sketch Sensore tattile hardware (saved by Fritzing 0.9.3b)
breadboards: 1

parts:
  Componente1 = Arduino Uno (Rev3)
  LED1 = LED - 5mm [color="Red (633nm)" package="5 mm [THT]"]
  R1 = Resistor [tolerance=±5% resistance=220 package="2010 [SMD]"]
  R2 = Resistor [tolerance=±5% resistance=220 package="2010 [SMD]"]

nets:
  N1: Componente1.D12/MISO, LED1.anode
  N2: Componente1.D2, R2.Pin_0
  N3: Componente1.D4, R2.Pin_1
  N4: Componente1.GND, R1.Pin_1
  N5: LED1.cathode, R1.Pin_0

notes:
  Qui c'è una piccola lamina di metallo.

// code stored in the sketch: Sensore_tattile_software.ino
#include <CapacitiveSensor.h>                                                                           //Importa la libreria CapacitiveSensor.
CapacitiveSensor Sensore_Tattile = CapacitiveSensor(4, 2);                                              //Crea un'istanza della libreria e dice i pin necessari.

int Soglia_Accensione_Led = 30;                                                                         //Soglia accensione led.
const int Pin_Led = 12;                                                                                 //Pin del led.

void setup() 
{
  Serial.begin(9600);                                                                                   //Apre il monitor seriale.
  pinMode(Pin_Led, OUTPUT);                                                                             //Definisce il pin del led come OUTPUT.
}

void loop() 
{
  long Valore_Sensore = Sensore_Tattile.capacitiveSensor(30);
  Serial.print("Valore sensore: ")                                                                      //Immagazzina nella variabile "Valore_Sensore" il valore del sensore. Legge 30 campioni.
  Serial.println(Valore_Sensore);                                                                       //Stampa sul monitor seriale il valore del sensore.
  if(Valore_Sensore > Soglia_Accensione_Led)
  {
    digitalWrite(Pin_Led, HIGH);
  }
else
{
  digitalWrite(Pin_Led, LOW);
}
delay(10);
}
