# Fritzing sketch Hackerare pulsanti hardware (saved by Fritzing 0.9.3b)
breadboards: 1

parts:
  Componente1 = Arduino Uno (Rev3)
  U1 = Optocoupler [package=THT]
  R1 = Resistor [tolerance=±5% resistance=220 package="2010 [SMD]"]

nets:
  N1: Componente1.D2, R1.Pin_0
  N2: Componente1.GND, U1.Pin_2
  N3: U1.Pin_1, R1.Pin_1

notes:
  Qua stanno i contatti esterni.
