# Fritzing sketch Tastiera arduino hardware (saved by Fritzing 0.9.3b)
breadboards: 1

parts:
  Componente1 = Arduino Uno (Rev3)
  J1 = Piezo Speaker
  S1 = Pushbutton [package="[SMD]"]
  S2 = Pushbutton [package="[SMD]"]
  S3 = Pushbutton [package="[SMD]"]
  S4 = Pushbutton [package="[SMD]"]
  R1 = Resistor [tolerance=±5% resistance=220 package=THT]
  R2 = Resistor [tolerance=±5% resistance=220 package=THT]
  R3 = Resistor [tolerance=±5% resistance=220 package=THT]
  R4 = Resistor [tolerance=±5% resistance=220 package=THT]

nets:
  N1: Componente1.A0, S1.Pin_1, S1.Pin_2, S2.Pin_1, S2.Pin_2, S3.Pin_1, S3.Pin_2, S4.Pin_1, S4.Pin_2, R4.Pin_0
  N2: Componente1.D8, J1.pin2
  N3: Componente1.5V, S1.Pin_3, S1.Pin_4, R1.Pin_1, R2.Pin_1
  N4: Componente1.GND, J1.pin1, R4.Pin_1
  N5: S2.Pin_3, S2.Pin_4, R1.Pin_0
  N6: S3.Pin_3, S3.Pin_4, R2.Pin_0
  N7: S4.Pin_3, S4.Pin_4, R3.Pin_0

notes:
  Le resistenze (da sinistra verso destra) sono da:
  220 Ohm;
  10 KOhm;
  1MOhm;
  10 KOhm.

// code stored in the sketch: Tastiera_arduino_software.ino
int Pulsanti[6] = {2};                        //Array di 6 numeri interi.       //Ad un numero intero assegno il valore 2.

int Note[] = {262,294,330,349};               //Array di quattro note musicali che corrispondono alle frequenze del DO, RE, MI, FA.

void setup()
{                         
  Serial.begin(9600);                         //Inizia comunicazione seriale con il computer.
}

void loop() 
{
  int Valore_Pin_A0 = analogRead(A0);         //Dichiarazione variabile locale per memorizzare il valore del pin A0.
  
  Serial.println(Valore_Pin_A0);              //Invio dei valori al computer.

  if(Valore_Pin_A0 == 1023)                   //Assegnamento dei valori a toni diversi.
  {                                           
    tone(8, Note[0]);
  }
  else if(Valore_Pin_A0 >= 990 && Valore_Pin_A0 <= 1010)
  {
    tone(8, Note[1]);
  }
  else if(Valore_Pin_A0 >= 505 && Valore_Pin_A0 <= 515)
  {
    tone(8, Note[2]);
  }
  else if(Valore_Pin_A0 >= 5 && Valore_Pin_A0 <= 10)
  {
    tone(8, Note[3]);
  }
  else
  {
    noTone(8);                              	//La funzione noTone è usata quando nessun pulsante viene premuto e quindi il piezo non suonerà.
  }
}
