# Fritzing sketch circuito (saved by Fritzing 0.9.3b)
breadboards: 1

parts:
  Componente1 = Arduino Uno (Rev3)
  R1 = Resistor [tolerance=±5% resistance=220 package=THT]
  R2 = Resistor [tolerance=±5% resistance=220 package=THT]
  R3 = Resistor [tolerance=±5% resistance=220 package=THT]
  R4 = Resistor [tolerance=±5% resistance=220 package=THT]
  S1 = Momentary Switch [package=ksa_sealed_tac_switch]
  S2 = Momentary Switch [package=ksa_sealed_tac_switch]
  S3 = Momentary Switch [package=ksa_sealed_tac_switch]
  S4 = Momentary Switch [package=ksa_sealed_tac_switch]
  LED1 = smd LED [color="Red (633nm)" package="1206 [SMD]"]
  LED2 = smd LED [color="Red (633nm)" package="0603 [SMD]"]
  LED3 = smd LED [color="Red (633nm)" package="0603 [SMD]"]
  LED4 = smd LED [color="Red (633nm)" package="0603 [SMD]"]
  R5 = Resistor [tolerance=±5% resistance=220 package=THT]
  R6 = Resistor [tolerance=±5% resistance=220 package=THT]
  R7 = Resistor [tolerance=±5% resistance=220 package=THT]
  R8 = Resistor [tolerance=±5% resistance=220 package=THT]

nets:
  N1: Componente1.D8, LED4.anode
  N2: Componente1.D9_PWM, LED3.anode
  N3: Componente1.D10_PWM/SS, LED2.anode
  N4: Componente1.D11_PWM/MOSI, LED1.anode
  N5: Componente1.D3_PWM, R4.Pin_0, S4.2
  N6: Componente1.D4, R3.Pin_0, S3.2
  N7: Componente1.D5_PWM, R2.Pin_0, S2.2
  N8: Componente1.D6_PWM, R1.Pin_0, S1.2
  N9: Componente1.5V, S1.4, S2.4, S3.4, S4.4
  N10: Componente1.GND, R1.Pin_1, R2.Pin_1, R3.Pin_1, R4.Pin_1, R5.Pin_1, R6.Pin_1, R7.Pin_1, R8.Pin_1
  N11: LED1.cathode, R5.Pin_0
  N12: LED2.cathode, R6.Pin_0
  N13: LED3.cathode, R7.Pin_0
  N14: LED4.cathode, R8.Pin_0
