# Fritzing sketch circuito (saved by Fritzing 0.9.3b)
breadboards: 1

parts:
  Componente1 = Arduino Ethernet Shield (Rev3)
  LED1 = smd LED [color="Red (633nm)" package="1206 [SMD]"]
  R1 = Resistor [tolerance=±5% resistance=220 package="2512 [SMD]"]

nets:
  N1: Componente1.GND, R1.Pin_1
  N2: Componente1.D7, LED1.anode
